// Logisim project alu.circ as structural Verilog: 1 circuit, main circuit alu
module alu (
  input  [31:0] A,
  input  [31:0] B,
  input  [3:0] ALUSel,
  output [31:0] Result
);

  wire slt7;
  wire [31:0] add0, and1, divu8, mul10, mulh14, mulhu11, or2, remu9, sll6, sra5, srl4, sub12, xor3;

  Adder #(.width(32)) adder_1 (.a(A), .b(B), .out(add0));  // open: cin, cout
  assign and1 = A & B;  // AND_Gate and_1, 32 bits wide
  assign or2 = A | B;  // OR_Gate or_1, 32 bits wide
  assign xor3 = A ^ B;  // XOR_Gate xor_1, 32 bits wide
  Shifter #(.width(32), .shift("lr")) shifter_1 (.in(A), .\dist (B[4:0]), .out(srl4));
  Shifter #(.width(32), .shift("ar")) shifter_2 (.in(A), .\dist (B[4:0]), .out(sra5));
  Shifter #(.width(32)) shifter_3 (.in(A), .\dist (B[4:0]), .out(sll6));
  Comparator #(.width(32)) comparator_1 (.a(A), .b(B), .lt(slt7));  // open: gt, eq
  Divider #(.width(32)) divider_1 (.a(A), .b(B), .out(divu8));  // open: upper, rem
  Divider #(.width(32)) divider_2 (.a(A), .b(B), .rem(remu9));  // open: out, upper
  Multiplier #(.width(32)) multiplier_1 (.a(A), .b(B), .cout(mulhu11));  // open: out, cin
  Subtractor #(.width(32)) subtractor_1 (.a(A), .b(B), .out(sub12));  // open: bin, bout
  xor xor_2 (mul10[31], A[31], B[31]);
  Multiplier #(.width(31)) multiplier_2 (.a(A[30:0]), .b(B[30:0]), .out(mul10[30:0]));  // open: cin, cout
  xor xor_3 (mulh14[31], A[31], B[31]);
  Multiplier #(.width(31)) multiplier_3 (.a(A[30:0]), .b(B[30:0]), .cout(mulh14[30:0]));  // open: out, cin
  Multiplexer #(.select(4), .width(32), .enable("false")) multiplexer_1 (
    .in0(add0), .in1(and1), .out(Result), .sel(ALUSel));  // open: in2, in3, in4, in5, in6, in7, in8, in9, in10, in11, in12, in13, in14, in15

  // Other names for the same wires on the sheet: bsel13[31:0] = B

  // Notes on the sheet:
  //   INPUTS to your circuit
  //   DON'T CHANGE THE LOCATIONS OF THE INPUTS AND OUTPUTS!
  //   OUTPUT from your circuit
endmodule
