// Logisim project cpu.circ as structural Verilog: 1 circuit, main circuit main
module main (
  input  [31:0] INSTRUCTION,
  input  CLOCK,
  output [31:0] PROGRAM_COUNTER,
  output [31:0] ra,
  output [31:0] sp,
  output [31:0] t0,
  output [31:0] t1,
  output [31:0] t2,
  output [31:0] s0,
  output [31:0] s1,
  output [31:0] a0
);

  wire control_logic_1_regwen, PCSel;
  wire [1:0] control_logic_1_wbsel;
  wire [2:0] control_logic_1_immsel, func3, undriven_2;
  wire [11:0] imm;
  wire [19:0] inst_pipeline;
  wire [31:0] adder_1_out, alu_output_pc, imm_output, mem_output, multiplexer_1_out, pc_pipeline, rs1_output,
       undriven, wb_value;

  Adder #(.width(32)) adder_1 (.a(PROGRAM_COUNTER), .b(32'h4), .out(adder_1_out));  // open: cin, cout
  Multiplexer #(.width(32), .enable("false")) multiplexer_1 (
    .in0(adder_1_out), .in1(alu_output_pc), .out(multiplexer_1_out), .sel(PCSel));
  Register #(.width(32)) PC (.D(multiplexer_1_out), .clk(CLOCK), .Q(PROGRAM_COUNTER));  // open: en, clr
  control_logic control_logic_1 (
    .RegWEn(control_logic_1_regwen), .ImmSel(control_logic_1_immsel), .PCSel(PCSel), .inst(undriven),
    .WBSel(control_logic_1_wbsel));  // open: BSel, ASel, BrUn, BrLt, BrEq, ALUSel, MemRW
  Register #(.width(32)) register_1 (.D(PROGRAM_COUNTER), .clk(CLOCK), .Q(pc_pipeline));  // open: en, clr
  Register #(.width(32)) register_2 (
    .D(INSTRUCTION), .clk(CLOCK), .Q({imm, inst_pipeline[19:15], func3, inst_pipeline[11:0]}));  // open: en, clr
  // branch_comp branch_comp_1: pin names not known
  imm_gen imm_gen_1 (
    .ImmSel(undriven_2), .imm(imm_output), .inst({imm, inst_pipeline[19:15], func3, inst_pipeline[11:0]}));
  regfile_main RegFile (
    .rd(inst_pipeline[11:7]), .Read_Data_1(rs1_output), .ra(ra), .sp(sp), .t0(t0), .t1(t1), .t2(t2), .s0(s0),
    .s1(s1), .a0(a0), .rs1(inst_pipeline[19:15]), .Write_Data(wb_value), .RegWEn(1'b1), .clk(CLOCK));  // open: rs2, Read_Data_2
  alu Arithmetic_Logic_Unit (.ALUSel(4'b0000), .Result(alu_output_pc), .A(rs1_output), .B(imm_output));
  // mem_main DMEM: pin names not known; wires that end beside it: CLOCK, mem_output
  Multiplexer #(.select(2), .width(32), .enable("false")) multiplexer_2 (
    .in0(pc_pipeline), .in1(alu_output_pc), .in2(mem_output), .out(wb_value), .sel(2'b01));  // open: in3

  // Other names for the same wires on the sheet: alu_output_wb[31:0] = alu_output_pc; clk = CLOCK;
  //   fetch_addr[31:0] = PROGRAM_COUNTER; opcode[6:0] = inst_pipeline[6:0]; rd[4:0] = inst_pipeline[11:7];
  //   inst_pipeline (some bits) = {imm, func3}; rs1[4:0] = inst_pipeline[19:15]

  // Notes on the sheet:
  //   Output
  //   IF Stage
  //   output from IMEM in run.circ
  //   IMEM (do **NOT** move this)
  //   input to IMEM in run.circ
  //   Inputs
  //   It is OK to move the PC, RegFile, ALU, MEM, Branch Comp, Imm Gen, and Control Logic to wherever is most convenient for you when constructing your CPU, and to delete this text
  //   Inputs/Outputs for testing. Do **NOT** move these.
  //   for addi (I format)
  //   ID Stage
endmodule
